# Fritzing sketch electronics0 - Copie (saved by Fritzing 1.0.4)
stripboards: 1

parts:
  Mod1 = Amica NodeMCU DEVKIT 1.0
  J2 = Basic Servo
  J3 = Dagu DGServo 9g header (male) [package=THT]
  J4 = male pin header, 2 pins [form="♂ (male)"]
  Yumo-enc1 = YumoE6B2
  J5 = male pin header, 4 pins [form="♂ (male)"]
  J6 = male pin header, 3 pins [form="♂ (male)"]

nets:
  3.3V: Mod1.pin1, Mod1.pin_10, Mod1.pin_26, J6.pin2
  GND: Mod1.pin2, Mod1.pin_9, Mod1.pin_25, Mod1.pin_29, J2.gnd, J3.gnd, J4.pin1, Yumo-enc1.GND, J5.pin1, J6.pin1
  N1: Mod1.pin_11, J6.pin3
  N2: Mod1.pin_13, Yumo-enc1.B, J5.pin4
  N3: Mod1.pin_14, Yumo-enc1.A, J5.pin3
  N4: Mod1.pin_15, J2.pulse, J3.pulse
  6V: Mod1.pin_30, J2.vcc, J3.Vcc, J4.pin2, Yumo-enc1.V, J5.pin2
