# Fritzing sketch electronics0 (saved by Fritzing 1.0.4)
circuit board: 8.46667cm x 5.64444cm
stripboards: 1

parts:
  H_OPTICAL = male pin header, 3 pins [form="♂ (male)"]
  H_ESPR = female pin header, 15 pins [form="♀ (female)"]
  H_ESPL = female pin header, 15 pins [form="♀ (female)"]
  H_GND_IN = male pin header, 1 pin [form="♂ (male)"]
  H_VCC_IN = male pin header, 1 pin [form="♂ (male)"]
  H_GND_OUT = male pin header, 1 pin [form="♂ (male)"]
  H_VCC_OUT = male pin header, 1 pin [form="♂ (male)"]
  J3 = Dagu DGServo 9g header (male) [package=THT]
  H_ENCODER = male pin header, 5 pins [form="♂ (male)"]
  Optical = KY-010 Photo Interrupter Module [package="Breakout board"]
  Yumo-enc1 = YumoE6B2
  M1 = RioRand LM2596
  Servo = Basic Servo
  ESP = NodeMCU V3.0

nets:
  GND: H_OPTICAL.pin1, H_ESPR.pin7, H_ESPR.pin14, H_ESPL.pin10, H_ESPL.pin14, H_GND_OUT.pin1, J3.gnd, H_ENCODER.pin1, H_ENCODER.pin2, Optical.-, Yumo-enc1.GND, M1.Pin_4, Servo.gnd, ESP.GND#6, ESP.GND#13, ESP.GND#16, ESP.GND#33
  3.3V: H_OPTICAL.pin2, H_ESPR.pin6, H_ESPR.pin15, H_ESPL.pin11, Optical.Vin, ESP.3V3
  N1: H_OPTICAL.pin3, H_ESPR.pin5, Optical.S, ESP.D4
  N2: H_ESPR.pin1, ESP.D0
  N3: H_ESPR.pin2, J3.pulse, Servo.pulse, ESP.D1
  N4: H_ESPR.pin3, ESP.D2
  N5: H_ESPR.pin4, ESP.D3
  N6: H_ESPR.pin8, ESP.D5
  N7: H_ESPR.pin9, H_ENCODER.pin5, Yumo-enc1.A, ESP.D6
  N8: H_ESPR.pin10, H_ENCODER.pin4, Yumo-enc1.B, ESP.D7
  N9: H_ESPR.pin11, ESP.D8
  N10: H_ESPR.pin12, ESP.RX
  N11: H_ESPR.pin13, ESP.TX
  N12: H_ESPL.pin1, ESP.A0
  N13: H_ESPL.pin2, ESP.GND#41
  N14: H_ESPL.pin3, ESP.VU
  N15: H_ESPL.pin4, ESP.SD3
  N16: H_ESPL.pin5, ESP.SD2
  N17: H_ESPL.pin6, ESP.SD1
  N18: H_ESPL.pin7, ESP.CMD
  N19: H_ESPL.pin8, ESP.SD0
  N20: H_ESPL.pin9, ESP.CLK
  N21: H_ESPL.pin12, ESP.EN
  N22: H_ESPL.pin13, ESP.RST
  6V: H_ESPL.pin15, H_VCC_OUT.pin1, J3.Vcc, H_ENCODER.pin3, Yumo-enc1.V, M1.Pin_3, Servo.vcc, ESP.Vin
  N23: H_GND_IN.pin1, M1.Pin_2
  N24: H_VCC_IN.pin1, M1.Pin_1

notes:
  ⨂

custom parts:
  KY-010 Photo Interrupter Module: Photo Interrupter Module Keyes KY-010 for Arduino, will trigger a signal when light between the sensor's gap is blocked.
  NodeMCU V3.0: NodeMcu V3 Lua WIFI Development Board
